# Fritzing sketch Capstone_Circuit_V1 (saved by Fritzing 0.9.3b)
breadboards: 1

parts:
  Part1 = Photon
  S1 = Pushbutton [package="[SMD]"]
  S2 = Momentary Switch [package=ksa_sealed_tac_switch]
  R1 = Resistor [tolerance=±5% resistance=10k package="0805 [SMD]"]
  R2 = Resistor [tolerance=±5% resistance=10k package="0805 [SMD]"]
  Adafruit_HUZZAH_ESP8266_Breakout1 = Adafruit HUZZAH ESP8266 Breakout [part_number=2471]

nets:
  N1: Part1.RX, Adafruit_HUZZAH_ESP8266_Breakout1.TX
  N2: Part1.TX, Adafruit_HUZZAH_ESP8266_Breakout1.RX
  GND: Part1.GND, R1.Pin_0, R2.Pin_0, Adafruit_HUZZAH_ESP8266_Breakout1.GND
  N3: Part1.D1, S2.4
  N4: Part1.D2, S1.Pin_3, S1.Pin_4, R2.Pin_1
  N5: Part1.3V3, S1.Pin_1, S1.Pin_2, S2.1, Adafruit_HUZZAH_ESP8266_Breakout1.V+
  N6: S2.3, R1.Pin_1

notes:
  This board is in lieu of Spec Digital sensor board (for which a fritzing stencil was not available) it was chosen because it has a similar interface with TX/RX, GND and V+/voltage
  Fritzing diagram for capstone project SEIS744
  Charles Christianson, Spring 2017
